# Fritzing sketch pirsensor (saved by Fritzing 0.9.3b)
breadboards: 1

parts:
  U1 = NodeMCU V1.0
  S1 = Momentary Switch [package=tactile-pth]
  PIR1 = PIR sensor
  R1 = Resistor [tolerance=±5% resistance=220 package=THT]
  R2 = Resistor [tolerance=±5% resistance=220 package=THT]
  LED1 = smd LED [color="Red (633nm)" package="0805 [SMD]"]

nets:
  N1: U1.D1, PIR1.SIG
  N2: U1.D2, LED1.anode
  N3: U1.3V3, S1.3
  GND: U1.GND, PIR1.GND, R1.Pin_1, R2.Pin_0
  N4: U1.RSV, PIR1.VDD
  N5: U1.A0, S1.1
  N6: S1.2, R1.Pin_0
  N7: R2.Pin_1, LED1.cathode

custom parts:
  NodeMCU V1.0: ESP8266 based NodeMCU
